// Logisim project ALU.circ as structural Verilog: 7 circuits, main circuit ALU
module ALU (
  input  [31:0] Operand_A,
  input  [31:0] Operand_B,
  input  [3:0] Selector,
  output [31:0] ALU_Output,
  output [31:0] High,
  output Zero_Flag,
  output Negative_Flag
);

  wire comparator_2_lt, comparator_3_lt;
  wire [31:0] Add, AND, DivHi, DivLo, DivuHigh, DivuLow, MultHi, MultLo, MuluHigh, MuluLow, NOR, OR, SLT,
       SLTU, Sub, XOR;

  Adder #(.width(32)) adder_1 (.a(Operand_A), .b(Operand_B), .out(Add));  // open: cin, cout
  Multiplier #(.width(32)) multiplier_1 (.a(Operand_A), .b(Operand_B), .out(MuluLow), .cout(MuluHigh));  // open: cin
  Comparator #(.width(32)) comparator_1 (.a({32{1'b0}}), .b(ALU_Output), .eq(Zero_Flag));  // open: gt, lt
  Signed_Mult signed_mult_1 (.Low(MultLo), .High(MultHi), .A(Operand_A), .B(Operand_B));
  Signed_Div signed_div_1 (.A(Operand_A), .Low(DivLo), .B(Operand_B), .High(DivHi));
  Multiplexer #(.select(4), .width(32), .enable("false")) multiplexer_1 (
    .in1(Add), .in2(Sub), .in3(AND), .in4(OR), .in5(NOR), .in6(XOR), .in7(SLT), .in8(SLTU), .in9(MuluLow),
    .in10(MultLo), .in11(DivLo), .in12(DivuLow), .out(ALU_Output), .sel(Selector));  // open: in0, in13, in14, in15
  Subtractor #(.width(32)) subtractor_1 (.a(Operand_A), .b(Operand_B), .out(Sub));  // open: bin, bout
  Divider #(.width(32)) divider_1 (.a(Operand_A), .b(Operand_B), .out(DivuLow), .rem(DivuHigh));  // open: upper
  assign OR = Operand_A | Operand_B;  // OR_Gate or_1, 32 bits wide
  // Probe on Operand_A
  // Probe on ALU_Output
  // Probe on High
  assign AND = Operand_A & Operand_B;  // AND_Gate and_1, 32 bits wide
  assign NOR = ~(Operand_A | Operand_B);  // NOR_Gate nor_1, 32 bits wide
  assign XOR = Operand_A ^ Operand_B;  // XOR_Gate xor_1, 32 bits wide
  // Probe on Operand_B
  // Probe on Selector
  Multiplexer #(.select(2), .width(32), .enable("false")) multiplexer_2 (
    .in0(MuluHigh), .in1(MultHi), .in2(DivHi), .in3(DivuHigh), .out(High), .sel(Selector[1:0]));
  Comparator #(.width(32)) comparator_2 (.a(Operand_A), .b(Operand_B), .lt(comparator_2_lt));  // open: gt, eq
  Comparator #(.width(32), .mode("unsigned")) comparator_3 (
    .a(Operand_A), .b(Operand_B), .lt(comparator_3_lt));  // open: gt, eq
  assign SLT = {{31{1'b0}}, comparator_2_lt};  // Bit_Extender bit_extender_1
  assign SLTU = {{31{1'b0}}, comparator_3_lt};  // Bit_Extender bit_extender_2

  assign Negative_Flag = ALU_Output[31];

  // Other names for the same wires on the sheet: A[31:0] = Operand_A; B[31:0] = Operand_B; HiResult[31:0] = High;
  //   OP[3:0] = Selector; OpHi[1:0] = Selector[1:0]; RESULT[31:0] = ALU_Output; N = ALU_Output[31]; Z = Zero_Flag

  // Notes on the sheet:
  //   INPUTS
  //   ARITHMETIC INSTRUCTIONS
  //   OUTPUTS
  //   LOGIC INSTRUCTIONS
  //   VISUALIZE INPUTS/OUTPUTS 
  //   COMPARISON INSTRUCTIONS
endmodule

module Signed_Mult (
  input  [31:0] A,
  input  [31:0] B,
  output [31:0] Low,
  output [31:0] High
);

  wire negator_1_carryout, signA, signB, signResult;
  wire [31:0] absolute_value_1_output, absolute_value_2_output, adder_1_out, negator_1_output, not_1_out,
       PosHi, PosLo;

  Absolute_Value absolute_value_1 (.A(A), .Output(absolute_value_1_output), .Negative(signA));
  Absolute_Value absolute_value_2 (.A(B), .Output(absolute_value_2_output), .Negative(signB));
  xor xor_1 (signResult, signA, signB);
  Multiplier #(.width(32)) multiplier_1 (
    .a(absolute_value_1_output), .b(absolute_value_2_output), .out(PosLo), .cout(PosHi));  // open: cin
  assign not_1_out = ~PosHi;  // NOT_Gate not_1, 32 bits wide
  Negator negator_1 (.A(PosLo), .Output(negator_1_output), .CarryOut(negator_1_carryout));
  Adder #(.width(32)) adder_1 (
    .a(not_1_out), .b({32{1'b0}}), .out(adder_1_out), .cin(negator_1_carryout));  // open: cout
  Multiplexer #(.width(32), .enable("false")) multiplexer_1 (
    .in0(PosLo), .in1(negator_1_output), .out(Low), .sel(signResult));
  Multiplexer #(.width(32), .enable("false")) multiplexer_2 (
    .in0(PosHi), .in1(adder_1_out), .out(High), .sel(signResult));

  // Other names for the same wires on the sheet: Hi[31:0] = High; Lo[31:0] = Low

  // Notes on the sheet:
  //   INPUTS
  //   OUTPUTS
endmodule

module Absolute_Value (
  input  [31:0] A,
  output [31:0] Output,
  output Negative
);

  wire [31:0] negator_1_output;

  Negator negator_1 (.A(A), .Output(negator_1_output));  // open: CarryOut
  Multiplexer #(.width(32), .enable("false")) multiplexer_1 (
    .in0(A), .in1(negator_1_output), .out(Output), .sel(A[31]));

  assign Negative = A[31];

  // Other names for the same wires on the sheet: Neg = A[31]; AbsVal[31:0] = Output

  // Notes on the sheet:
  //   INPUTS
  //   OUTPUTS
endmodule

module Signed_Div (
  input  [31:0] A,
  input  [31:0] B,
  output [31:0] Low,
  output [31:0] High
);

  wire signA, signB, signResult;
  wire [31:0] absolute_value_1_output, absolute_value_2_output, negator_1_output, negator_2_output, PosHi,
       PosLo;

  Absolute_Value absolute_value_1 (.A(A), .Output(absolute_value_1_output), .Negative(signA));
  Absolute_Value absolute_value_2 (.A(B), .Output(absolute_value_2_output), .Negative(signB));
  xor xor_1 (signResult, signA, signB);
  Divider #(.width(32)) divider_1 (
    .a(absolute_value_1_output), .b(absolute_value_2_output), .out(PosLo), .rem(PosHi));  // open: upper
  Negator negator_1 (.A(PosLo), .Output(negator_1_output));  // open: CarryOut
  Negator negator_2 (.A(PosHi), .Output(negator_2_output));  // open: CarryOut
  Multiplexer #(.width(32), .enable("false")) multiplexer_1 (
    .in0(PosLo), .in1(negator_1_output), .out(Low), .sel(signResult));
  Multiplexer #(.width(32), .enable("false")) multiplexer_2 (
    .in0(PosHi), .in1(negator_2_output), .out(High), .sel(signResult));

  // Other names for the same wires on the sheet: Hi[31:0] = High; Lo[31:0] = Low

  // Notes on the sheet:
  //   INPUTS
  //   OUTPUTS
endmodule

module Negator (
  input  [31:0] A,
  output [31:0] Output,
  output CarryOut
);

  wire [31:0] not_1_out;

  assign not_1_out = ~A;  // NOT_Gate not_1, 32 bits wide
  Adder #(.width(32)) adder_1 (.a(not_1_out), .b(32'h1), .out(Output), .cout(CarryOut));  // open: cin

  // Other names for the same wires on the sheet: NegVal[31:0] = Output

  // Notes on the sheet:
  //   INPUTS
  //   OUTPUTS
endmodule

module ALU_INPUT (
  input  [31:0] RT,
  input  [15:0] Const,
  input  Const_Extender_Selector,
  input  Type_I,
  output [31:0] B
);

  wire [31:0] Const_t;

  CONST_EXTEND const_extend_1 (.Const(Const), .Selector(Const_Extender_Selector), .Const_Extended(Const_t));
  Multiplexer #(.width(32), .enable("false")) multiplexer_1 (.in0(RT), .in1(Const_t), .out(B), .sel(Type_I));

  // Other names for the same wires on the sheet: ALU_IN[31:0] = B; EXTSEL = Const_Extender_Selector

  // Notes on the sheet:
  //   INPUT
  //   ALU INPUT SELECTION
  //   OUTPUT
endmodule

module CONST_EXTEND (
  input  [15:0] Const,
  input  Selector,
  output [31:0] Const_Extended
);

  wire and_1_out;

  and and_1 (and_1_out, ~Selector, Const[15]);  // AND_Gate
  assign Const_Extended = {{16{and_1_out}}, Const};  // Bit_Extender bit_extender_1

  // Other names for the same wires on the sheet: I15 = Const[15]; EXTENDED[31:0] = Const_Extended; SEL = Selector

  // Notes on the sheet:
  //   INPUT
  //   CONST EXTENSION
  //   OUTPUT
endmodule
