// Logisim project DATA_PATH.circ as structural Verilog: 1 circuit, main circuit DATA_PATH
module DATA_PATH (
  input  Pop,
  input  Push,
  input  [31:0] RAM_Data,
  input  RF_R_W,
  input  Type_I,
  input  KBD_Available,
  input  [15:0] Const,
  input  Store_Word,
  input  Enable_PC,
  input  [6:0] Keyboard,
  input  Const_Extend_Sel,
  input  Enable_HI_LO,
  input  [4:0] Data_Adress,
  input  [4:0] Selector_A,
  input  Reset,
  input  [4:0] Selector_B,
  input  Clk,
  input  [3:0] ALU_Op_Selector,
  input  [2:0] RF_Input_Selector,
  output [31:0] RAM_Write_Data,
  output [31:0] RS,
  output [31:0] RT,
  output [31:0] SP,
  output [31:0] ALU_Out,
  output [6:0] tty_Data
);

  wire [31:0] alu_input_1_alu_input, HI_IN, HI_OUT, LO_OUT, rf_input_1_rf_input;

  RF_INPUT rf_input_1 (
    .RAM_Data(RAM_Data), .Keyboard(Keyboard), .ALU_Output(ALU_Out), .Selector(RF_Input_Selector),
    .HI(HI_OUT), .Clock(Clk), .LO(LO_OUT), .KBD_Available(KBD_Available), .RF_Input(rf_input_1_rf_input));
  ALU_INPUT alu_input_1 (
    .RT(RT), .Const(Const), .Const_Ext_Sel(Const_Extend_Sel), .Type_I(Type_I),
    .ALU_Input(alu_input_1_alu_input));
  Register_File register_file_1 (
    .Data_Input(rf_input_1_rf_input), .reset(Reset), .R_W(RF_R_W), .clock(Clk), .A(RS), .B(RT),
    .Data_Address(Data_Adress), .Selector_A(Selector_A), .Selector_B(Selector_B), .push(Push), .pop(Pop),
    .Stack_Pointer(SP), .PC_enable(Enable_PC));
  ALU alu_1 (
    .Data_A(RS), .Data_B(alu_input_1_alu_input), .ALU_Output(ALU_Out), .High(HI_IN),
    .Selector(ALU_Op_Selector));
  HI_LO_Registers hi_lo_registers_1 (
    .HI_in(HI_IN), .OutputHi(HI_OUT), .Lo_in(ALU_Out), .OutputLo(LO_OUT), .HI_LO_enable(Enable_HI_LO),
    .Clock(Clk));
  Multiplexer #(.width(32), .disabled(0), .enable("false")) multiplexer_1 (
    .in0(RS), .in1(RT), .out(RAM_Write_Data), .sel(Store_Word));

  assign tty_Data = RS[6:0];

  // Other names for the same wires on the sheet: ALU[31:0] = ALU_Out; ALU_OP_SEL[3:0] = ALU_Op_Selector;
  //   CES = Const_Extend_Sel; DATA_ADS[4:0] = Data_Adress; HI_LO_EN = Enable_HI_LO; KBD[6:0] = Keyboard;
  //   KBD_AV = KBD_Available; PC_EN = Enable_PC; R_W = RF_R_W; RAM_WD[31:0] = RAM_Write_Data;
  //   RF_IN_SEL[2:0] = RF_Input_Selector; RST = Reset; SEL_A[4:0] = Selector_A; SEL_B[4:0] = Selector_B;
  //   SW = Store_Word

  // Notes on the sheet:
  //   DATA INPUT
  //   SELECTORS
  //   INPUTS
  //   REGISTER FILE
  //   ALU
  //   FLAGS
  //   SPECIAL
  //   OUTPUT
  //   HI/LO REGISTER
  //   TERMINAL
endmodule
