// Logisim project MA_INPUT_SELECTOR.circ as structural Verilog: 1 circuit, main circuit MA_INPUT_SELECTOR
module MA_INPUT_SELECTOR (
  input  pop,
  input  push,
  input  sw,
  input  lw,
  input  isInst,
  output [1:0] BC_SELECTOR
);

  or or_1 (BC_SELECTOR[1], pop, isInst, push);
  or or_2 (BC_SELECTOR[0], sw, isInst, lw);

  // Other names for the same wires on the sheet: INST = isInst; SELECTOR[1:0] = BC_SELECTOR

  // Notes on the sheet:
  //   INPUTS
  //   BIT 0
  //   SW
  //   Or
  //   LW
  //   Or
  //   MA_SELECTION
  //   OUTPUTS
  //   SELECTOR CODES
  //   BIT 1
  //   POP
  //   Or
  //   PUSH
  //   Or
endmodule
