// Logisim project RAM_ACCESS.circ as structural Verilog: 1 circuit, main circuit RAM_ACCESS
module RAM_ACCESS (
  input  [31:0] RAM_Output_0,
  input  [31:0] Data_Input,
  input  [31:0] RAM_Address,
  input  [31:0] RAM_Output_1,
  input  [3:0] Read_Time,
  input  [31:0] RAM_Output_2,
  input  [3:0] Write_Time,
  input  [31:0] RAM_Output_3,
  input  Clk,
  input  Write,
  input  Rst,
  input  Read,
  output [31:0] RAM_Input_0,
  output [31:0] Data_Output,
  output [31:0] RAM_Input_1,
  output [15:0] Address,
  output [3:0] Mask,
  output [31:0] RAM_Input_2,
  output CS,
  output R_W,
  output Ready_Read,
  output [31:0] RAM_Input_3,
  output Ready_Write
);

  wire CSR, write_ram_1_p7, write_ram_1_p9;

  READ_RAM read_ram_1 (
    .Bank_0(RAM_Output_0), .RAM_Address(RAM_Address), .Read_Time(Read_Time), .Bank_1(RAM_Output_1),
    .Clk(Clk), .Rst(Rst), .Bank_2(RAM_Output_2), .Get(Read), .Bank_3(RAM_Output_3), .Data(Data_Output),
    .Ready(Ready_Read), .Chip_Sel(CSR));
  // WRITE_RAM write_ram_1: pin names not known; wires that end beside it: Rst, Write, Write_Time, Data_Input, RAM_Address, Clk, write_ram_1_p7, write_ram_1_p7, write_ram_1_p9, write_ram_1_p9, RAM_Input_0, RAM_Input_1, RAM_Input_2, RAM_Input_3, Ready_Write, R_W
  Demultiplexer #(.select(2), .enable("false")) demultiplexer_1 (
    .out0(Mask[0]), .out1(Mask[1]), .out2(Mask[2]), .out3(Mask[3]), .in(1'b1), .sel(RAM_Address[3:2]));
  or or_1 (CS, CSR, R_W);

  assign Address = RAM_Address[19:4];

  // Other names for the same wires on the sheet: CSW = R_W; DIN[31:0] = Data_Input; DOU[31:0] = Data_Output;
  //   IN0[31:0] = RAM_Input_0; IN1[31:0] = RAM_Input_1; IN2[31:0] = RAM_Input_2; IN3[31:0] = RAM_Input_3;
  //   OU0[31:0] = RAM_Output_0; OU1[31:0] = RAM_Output_1; OU2[31:0] = RAM_Output_2; OU3[31:0] = RAM_Output_3;
  //   RA[31:0] = RAM_Address; ADR[15:0] = RAM_Address[19:4]; RR = Ready_Read; RT[3:0] = Read_Time;
  //   RWrite = Ready_Write; WT[3:0] = Write_Time

  // Notes on the sheet:
  //   RAM OUTPUT
  //   INPUT
  //   READ to RAM
  //   DATA INPUT and RAM ADDRESS
  //   TIMING
  //   CONTROL
  //   WRITE to RAM
  //   RAM INPUT
  //   OUTPUT
  //   ADDRESS and MASK
  //   CHIP SET and R/W
  //   DATA OUTPUT
  //   ADDRESS and MASK
  //   CONTROL
endmodule
