// Logisim project WRITE_RAM.circ as structural Verilog: 1 circuit, main circuit WRITE_RAM
module WRITE_RAM (
  input  [31:0] Data,
  input  [31:0] RAM_Addr,
  input  [3:0] Write_Time,
  input  Clk,
  input  Rst,
  input  Write,
  output [31:0] Bank_0,
  output [31:0] Bank_1,
  output Ready,
  output [31:0] Bank_2,
  output RWrite,
  output [31:0] Bank_3
);

  wire demultiplexer_1_out0, demultiplexer_1_out1, or_1_out, or_2_out, TIMER;
  wire [31:0] reverse_1_data_reverse;

  or or_1 (or_1_out, demultiplexer_1_out0, Write);
  D_Flip_Flop d_ff_1 (.clk(Clk), .D(or_1_out), .Q(Ready), .reset(Rst));  // open: Qn, preset, en
  or or_2 (or_2_out, RWrite, Rst);
  Demultiplexer #(.enable("false")) demultiplexer_1 (
    .out0(demultiplexer_1_out0), .out1(demultiplexer_1_out1), .in(Ready), .sel(TIMER));
  REVERSE reverse_1 (.Data_Input(Data), .Data_Reverse(reverse_1_data_reverse));
  Demultiplexer #(.select(2), .width(32), .enable("false")) demultiplexer_2 (
    .out0(Bank_0), .out1(Bank_1), .out2(Bank_2), .out3(Bank_3), .in(reverse_1_data_reverse),
    .sel(RAM_Addr[3:2]));
  TIMER timer_1 (.Wait_Time(Write_Time), .Rst(or_2_out), .Clk(Clk), .Start(Ready), .Ready(TIMER));
  D_Flip_Flop SAVE (.clk(Clk), .D(demultiplexer_1_out1), .Q(RWrite), .reset(Rst));  // open: Qn, preset, en

  // Other names for the same wires on the sheet: BANK0[31:0] = Bank_0; BANK1[31:0] = Bank_1; BANK2[31:0] = Bank_2;
  //   BANK3[31:0] = Bank_3; SEL[1:0] = RAM_Addr[3:2]; RW = Ready; WT[3:0] = Write_Time

  // Notes on the sheet:
  //   INPUT
  //   AUXILIAR INPUTS
  //   READ DATA
  //   REVERSE RAM DATA
  //   TIMER
  //   OUTPUT
endmodule
